# Fritzing sketch timekeeper (saved by Fritzing 0.9.3b)

parts:
  MCU1 = Raspberry Pi Zero
  Q2 = LTR-301 [package=ltr-301]
  D1 = LTE-302 [package=lte-302]

nets:
  N1: MCU1.pin_1, MCU1.pin_17, D1.A
  N2: MCU1.pin_6, MCU1.pin_39, Q2.E, D1.C
  N3: MCU1.pin_13, Q2.C
